# Fritzing sketch components-hwserial (saved by Fritzing 0.9.1b)
breadboards: 1

parts:
  Part3 = Triple Axis Accelerometer Breakout - ADXL345
  Part4 = BlinkM
  GPS1 = Adafruit Ultimate GPS Breakout
  Part5 = Arduino Mega ADK (Rev3)

nets:
  GND: Part3.GND, Part4.GND, GPS1.GND, Part5.GND
  VCC: Part3.VCC, Part4.VCC, GPS1.VIN, Part5.5V
  N1: Part3.SDA, Part4.SDA, Part5.D20/SDA
  N2: Part3.SCL, Part4.SCL, Part5.D21/SCL
  N3: GPS1.TX, Part5.D19/RX1

custom parts:
  BlinkM: BlinkM component
