# Fritzing sketch components-no-swserial (saved by Fritzing 0.9.1b)
breadboards: 1

parts:
  Part1 = Arduino Uno (Rev3) - ICSP
  Part3 = Triple Axis Accelerometer Breakout - ADXL345
  Part4 = BlinkM

nets:
  N1: Part1.A4/SDA, Part3.SCL, Part4.SCL
  N2: Part1.A5/SCL, Part3.SDA, Part4.SDA
  GND: Part1.GND, Part3.GND, Part4.GND
  N3: Part1.D8, Part1.D9_PWM
  N4: Part1.D5_PWM, Part1.D6_PWM
  VCC: Part1.5V, Part3.VCC, Part4.VCC

custom parts:
  BlinkM: BlinkM component
